// Logisim project y86.circ as structural Verilog: 12 circuits, main circuit regwriter
module dpath (
  input  in_1,
  input  in_2,
  input  in_3,
  input  [1:0] in_4,
  input  in_5,
  input  in_6,
  input  [1:0] in_7,
  input  [1:0] in_8,
  input  in_9,
  input  [1:0] in_10,
  input  in_11,
  input  in_12,
  input  in_13,
  input  in_14,
  input  in_15,
  input  in_16,
  input  _0_add,
  input  in_18,
  input  in_19,
  input  rB____F,
  input  Reset,
  input  in_22,
  output out_23
);

  wire and_1_out, cnd_1_cnd, comparator_1_eq, comparator_2_eq, D_RAMread, D_RAMuse, D_RAMWrite, DMemReady,
       Exception, I_RAMread, I_RAMuse, IMemReady, ioshim_1_kb_clear, ioshim_1_kb_clock, ioshim_1_tty_clear,
       ioshim_1_tty_enable, kbyte_buddy_1_sel, kbyte_buddy_2_sel, keyboard_1_avail, ldPriv,
       multiplexer_8_out, newPCsel2, not_1_out, or_1_out, or_2_out, or_3_out, PrivMode, PrivSel,
       regreader_1_clr, regreader_1_clr_2, regreader_1_clr_3, regreader_1_clr_4, regreader_1_clr_5,
       regreader_1_clr_6, regreader_1_clr_7, regreader_1_clr_8, regwriter_1_en, regwriter_1_en_2,
       regwriter_1_en_3, regwriter_1_en_4, regwriter_1_en_5, regwriter_1_en_6, regwriter_1_en_7,
       regwriter_1_en_8;
  wire [0:0] rom_2_data;
  wire [2:0] alu_1_cc, bit_extender_1_out, bit_extender_2_out, bit_extender_3_out, bit_extender_4_out, cc;
  wire [3:0] icode, ifun, isplit_1_ra, isplit_1_rb, multiplexer_5_out, multiplexer_6_out, multiplexer_7_out,
       multiplexer_11_out;
  wire [5:0] Current_State_q, useq_1_nextstate;
  wire [6:0] ioshim_1_out_13, keyboard_1_data;
  wire [7:0] D_Data_from_RAM, D_Data_to_RAM, I_Data_from_RAM, ioshim_1_out_12, ishim_1_out_6, ishim_1_out_7,
       ishim_1_out_8, ishim_1_out_9, ishim_1_out_10, ishim_1_out_11, ram_1_data, rom_1_data, rom_3_data;
  wire [9:0] kbyte_buddy_1_ram_addr, kbyte_buddy_2_ram_addr;
  wire [31:0] adder_1_out, alu_1_vale, buffer_1_out, controlled_buffer_1_out, D_RAMAddr, dhsim_1_dataout,
       eax_q, ebp_q, ebx_q, ecx_q, edi_q, edx_q, esi_q, esp_q, I_RAMAddr, isplit_1_d_v, isplit_1_dest, MAR_q,
       MDR_q, multiplexer_1_out, multiplexer_2_out, multiplexer_3_out, multiplexer_4_out, multiplexer_9_out,
       multiplexer_10_out, multiplexer_12_out, multiplexer_13_out, PC_q, regreader_1_vala, regreader_1_valb,
       regwriter_1_d0, regwriter_1_d1, regwriter_1_d2, regwriter_1_d3, regwriter_1_d4, regwriter_1_d5,
       regwriter_1_d6, regwriter_1_d7;

  Register #(.width(32)) PC (.D(multiplexer_3_out), .en(in_11), .Q(PC_q), .clk(out_23), .clr(Reset));
  Clock #(.highDuration(16), .lowDuration(16)) Clock (.out(out_23));
  // Probe on I_RAMuse
  // Probe on I_RAMAddr
  // Probe on in_12
  // Probe on in_4
  // Probe on multiplexer_1_out
  Multiplexer #(.select(2), .width(32), .enable("false")) multiplexer_1 (
    .in0(32'h1), .in1(32'h2), .in2(32'h5), .in3(32'h6), .out(multiplexer_1_out), .sel(in_4));
  // Probe on I_RAMread
  // Probe on in_19
  Adder #(.width(32)) adder_1 (.a(multiplexer_1_out), .b(PC_q), .out(adder_1_out));  // open: cin, cout
  CND cnd_1 (.ZSO(cc), .ifun(ifun), .CND(cnd_1_cnd));
  // Probe on IMemReady
  // Probe on I_Data_from_RAM
  // Probe on in_18
  Multiplexer #(.width(32), .enable("false")) multiplexer_2 (
    .in0(adder_1_out), .in1(multiplexer_4_out), .out(multiplexer_2_out), .sel(cnd_1_cnd));
  // Probe on newPCsel2
  isplit isplit_1 (
    .B0(ishim_1_out_6), .B1(ishim_1_out_7), .B2(ishim_1_out_8), .B3(ishim_1_out_9), .B4(ishim_1_out_10),
    .B5(ishim_1_out_11), .icode(icode), .ifun(ifun), .rA(isplit_1_ra), .rB(isplit_1_rb),
    .Dest(isplit_1_dest), .D_V(isplit_1_d_v));
  ishim ishim_1 (
    .in_2(PC_q), .out_6(ishim_1_out_6), .out_7(ishim_1_out_7), .out_8(ishim_1_out_8), .out_9(ishim_1_out_9),
    .out_10(ishim_1_out_10), .out_11(ishim_1_out_11), .done(IMemReady), .req(in_12), .reset(Reset),
    .clock(out_23), .RAMuse(I_RAMuse), .out_14(I_RAMAddr), .RAMread(I_RAMread), .in_5(I_Data_from_RAM));
  // Probe on rB____F
  // Probe on in_6
  Multiplexer #(.select(3), .width(32), .enable("false")) multiplexer_3 (
    .in0(adder_1_out), .in1(multiplexer_4_out), .in2(dhsim_1_dataout), .in3(multiplexer_2_out),
    .in4(32'h100), .in5(32'h200), .out(multiplexer_3_out), .sel({newPCsel2, in_7}));  // open: in6, in7
  // Probe on icode
  // Probe on ifun
  Multiplexer #(.width(32), .enable("false")) multiplexer_4 (
    .in0(isplit_1_dest), .in1(isplit_1_d_v), .out(multiplexer_4_out), .sel(in_19));
  // Probe on multiplexer_4_out
  // Probe on in_10
  Register #(.width(6)) Current_State (
    .D(useq_1_nextstate), .Q(Current_State_q), .clk(out_23), .clr(Reset));  // open: en
  // Probe on isplit_1_ra
  // Probe on isplit_1_rb
  // Probe on in_15
  Multiplexer #(.width(4), .enable("false")) multiplexer_5 (
    .in0(isplit_1_rb), .in1(4'b0100), .out(multiplexer_5_out), .sel(in_6));
  Multiplexer #(.width(4), .enable("false")) multiplexer_6 (
    .in0(isplit_1_ra), .in1(4'b0100), .out(multiplexer_6_out), .sel(in_18));
  Multiplexer #(.width(4), .enable("false")) multiplexer_7 (
    .in0(isplit_1_rb), .in1(4'b0100), .out(multiplexer_7_out), .sel(rB____F));
  // Probe on in_8
  Bit_Extender #(.in_width(4), .out_width(3)) bit_extender_1 (.in(multiplexer_5_out), .out(bit_extender_1_out));
  Multiplexer #(.select(2), .enable("false")) multiplexer_8 (
    .in0(1'b0), .in1(1'b1), .in2(cnd_1_cnd), .out(multiplexer_8_out), .sel(in_10));  // open: in3
  Bit_Extender #(.in_width(4), .out_width(3)) bit_extender_2 (.in(isplit_1_ra), .out(bit_extender_2_out));
  Bit_Extender #(.in_width(4), .out_width(3)) bit_extender_3 (.in(multiplexer_6_out), .out(bit_extender_3_out));
  Bit_Extender #(.in_width(4), .out_width(3)) bit_extender_4 (.in(multiplexer_7_out), .out(bit_extender_4_out));
  Comparator #(.width(4)) comparator_1 (.a(multiplexer_7_out), .b(4'b1111), .eq(comparator_1_eq));  // open: gt, lt
  // Probe on in_13
  ROM #(.addrWidth(6), .dataWidth(32)) rom_1 (
    .addr(Current_State_q),
    .data({in_12, in_4, in_19, in_18, rB____F, in_6, in_10, in_15, in_8, in_13, _0_add, in_2, in_14, in_16, in_5, in_9, in_1, in_3, in_7, in_11, rom_1_data}),
    .sel(1'b1));
  Register #(.width(32)) eax (.D(regwriter_1_d0), .en(regwriter_1_en), .Q(eax_q), .clk(out_23), .clr(regreader_1_clr));
  regwriter regwriter_1 (
    .dstE(bit_extender_1_out), .reqE(multiplexer_8_out), .dstM(bit_extender_2_out), .reqM(in_15),
    .valE(alu_1_vale), .valM(dhsim_1_dataout), .D0(regwriter_1_d0), .EN(regwriter_1_en), .D1(regwriter_1_d1),
    .EN_2(regwriter_1_en_2), .D2(regwriter_1_d2), .EN_3(regwriter_1_en_3), .D3(regwriter_1_d3),
    .EN_4(regwriter_1_en_4), .D4(regwriter_1_d4), .EN_5(regwriter_1_en_5), .D5(regwriter_1_d5),
    .EN_6(regwriter_1_en_6), .D6(regwriter_1_d6), .EN_7(regwriter_1_en_7), .D7(regwriter_1_d7),
    .EN_8(regwriter_1_en_8));
  Register #(.width(32)) ecx (
    .D(regwriter_1_d1), .en(regwriter_1_en_2), .Q(ecx_q), .clk(out_23), .clr(regreader_1_clr_2));
  Register #(.width(32)) edx (
    .D(regwriter_1_d2), .en(regwriter_1_en_3), .Q(edx_q), .clk(out_23), .clr(regreader_1_clr_3));
  Register #(.width(32)) ebx (
    .D(regwriter_1_d3), .en(regwriter_1_en_4), .Q(ebx_q), .clk(out_23), .clr(regreader_1_clr_4));
  Register #(.width(32)) esp (
    .D(regwriter_1_d4), .en(regwriter_1_en_5), .Q(esp_q), .clk(out_23), .clr(regreader_1_clr_5));
  Register #(.width(32)) ebp (
    .D(regwriter_1_d5), .en(regwriter_1_en_6), .Q(ebp_q), .clk(out_23), .clr(regreader_1_clr_6));
  Register #(.width(32)) esi (
    .D(regwriter_1_d6), .en(regwriter_1_en_7), .Q(esi_q), .clk(out_23), .clr(regreader_1_clr_7));
  Register #(.width(32)) edi (
    .D(regwriter_1_d7), .en(regwriter_1_en_8), .Q(edi_q), .clk(out_23), .clr(regreader_1_clr_8));
  // Probe on _0_add
  regreader regreader_1 (
    .srcA(bit_extender_3_out), .srcB(bit_extender_4_out), .valA(regreader_1_vala), .valB(regreader_1_valb),
    .reset(Reset), .CLR(regreader_1_clr), .Q(eax_q), .CLR_2(regreader_1_clr_2), .Q_2(ecx_q),
    .CLR_3(regreader_1_clr_3), .Q_3(edx_q), .CLR_4(regreader_1_clr_4), .Q_4(ebx_q),
    .CLR_5(regreader_1_clr_5), .Q_5(esp_q), .CLR_6(regreader_1_clr_6), .Q_6(ebp_q),
    .CLR_7(regreader_1_clr_7), .Q_7(esi_q), .CLR_8(regreader_1_clr_8), .Q_8(edi_q));
  // Probe on in_2
  ROM #(.addrWidth(6), .dataWidth(4)) rom_2 (
    .addr(Current_State_q), .data({ldPriv, PrivSel, newPCsel2, rom_2_data[0]}), .sel(1'b1));
  // Probe on regreader_1_vala
  // Probe on regreader_1_valb
  // Probe on multiplexer_4_out
  // Probe on in_16
  // Probe on in_14
  Multiplexer #(.select(2), .width(32), .enable("false")) multiplexer_9 (
    .in0(regreader_1_vala), .in1(multiplexer_4_out), .in2(32'h4), .in3(32'hfffffffc),
    .out(multiplexer_9_out), .sel(in_8));
  or or_1 (or_1_out, comparator_1_eq, in_13);
  // Probe on in_5
  alu alu_1 (
    .ALU_A(multiplexer_9_out), .CC(alu_1_cc), .ALU_B(multiplexer_10_out), .valE(alu_1_vale),
    .ALU_op(multiplexer_11_out));
  Multiplexer #(.width(32), .enable("false")) multiplexer_10 (
    .in0(regreader_1_valb), .in1({32{1'b0}}), .out(multiplexer_10_out), .sel(or_1_out));
  Multiplexer #(.width(4), .enable("false")) multiplexer_11 (
    .in0(4'b0000), .in1(ifun), .out(multiplexer_11_out), .sel(_0_add));
  // Probe on in_9
  // Probe on in_1
  Register #(.width(3)) u_CC (.D(alu_1_cc), .en(in_2), .Q(cc), .clk(out_23), .clr(Reset));
  // Probe on cc
  // Probe on in_3
  // Probe on icode
  // Probe on adder_1_out
  // Probe on alu_1_vale
  Multiplexer #(.width(32), .enable("false")) multiplexer_12 (
    .in0(regreader_1_vala), .in1(adder_1_out), .out(multiplexer_12_out), .sel(in_5));
  Multiplexer #(.width(32), .enable("false")) multiplexer_13 (
    .in0(alu_1_vale), .in1(regreader_1_vala), .out(multiplexer_13_out), .sel(in_14));
  // Probe on in_7
  Register #(.width(32)) MDR (.D(multiplexer_12_out), .en(in_9), .Q(MDR_q), .clk(out_23), .clr(Reset));
  Register #(.width(32)) MAR (.D(multiplexer_13_out), .en(in_16), .Q(MAR_q), .clk(out_23), .clr(Reset));
  // Probe on in_11
  useq useq_1 (
    .CurrentState(Current_State_q), .Select(rom_1_data[7:6]), .icode(icode), .valN(rom_1_data[5:0]),
    .DMemDone(DMemReady), .IMemDone(IMemReady), .NextState(useq_1_nextstate), .Exception(Exception));
  // Probe on D_RAMuse
  // Probe on D_RAMAddr
  // Probe on newPCsel2
  // Probe on dhsim_1_dataout
  // Probe on D_RAMread
  // Probe on D_RAMWrite
  // Probe on D_Data_to_RAM
  // Probe on PrivSel
  // Probe on ldPriv
  dhsim dhsim_1 (
    .in_1(MAR_q), .in_3(MDR_q), .DataOut(dhsim_1_dataout), .out_9(D_Data_to_RAM), .RAMwrite(D_RAMWrite),
    .RAMread(D_RAMread), .done(DMemReady), .DMem_Write(in_3), .req(in_1), .reset(Reset), .clock(out_23),
    .RAMuse(D_RAMuse), .out_14(D_RAMAddr), .in_2(D_Data_from_RAM));
  // Probe on D_Data_from_RAM
  // Probe on PrivMode
  D_Flip_Flop d_ff_1 (.clk(out_23), .D(PrivSel), .Q(PrivMode), .en(ldPriv), .reset(Reset));  // open: Qn, preset
  // Probe on Exception
  // Probe on dhsim_1_dataout
  // Probe on DMemReady
  // Probe on buffer_1_out
  // Probe on controlled_buffer_1_out
  assign controlled_buffer_1_out = I_RAMuse ? I_RAMAddr : 32'bz;  // Controlled_Buffer controlled_buffer_1
  or or_2 (or_2_out, I_RAMuse, D_RAMuse);
  assign controlled_buffer_1_out = D_RAMuse ? D_RAMAddr : 32'bz;  // Controlled_Buffer controlled_buffer_2
  assign buffer_1_out = controlled_buffer_1_out;  // Buffer buffer_1, 32 bits wide
  // Probe on ioshim_1_out_12
  not not_1 (not_1_out, or_2_out);
  assign buffer_1_out = not_1_out ? {32{1'b0}} : 32'bz;  // Controlled_Buffer controlled_buffer_3
  // Probe on D_Data_to_RAM
  kbyte_buddy kbyte_buddy_1 (
    .addr(controlled_buffer_1_out), .addr_prefix({32{1'b0}}), .\use (or_2_out),
    .ram_addr(kbyte_buddy_1_ram_addr), .sel(kbyte_buddy_1_sel));
  kbyte_buddy kbyte_buddy_2 (
    .addr(controlled_buffer_1_out), .addr_prefix(32'h400), .\use (or_2_out),
    .ram_addr(kbyte_buddy_2_ram_addr), .sel(kbyte_buddy_2_sel));
  and and_1 (and_1_out, or_2_out, ~PrivMode);  // AND_Gate
  or or_3 (or_3_out, I_RAMread, D_RAMread);
  Comparator #(.width(28)) comparator_2 (.a(28'hfffe0), .b(buffer_1_out[31:4]), .eq(comparator_2_eq));  // open: gt, lt
  ioshim ioshim_1 (
    .RAM_Use(and_1_out), .in_4(buffer_1_out), .in_5(D_Data_to_RAM), .RAM_Read(or_3_out),
    .RAM_Write(D_RAMWrite), .reset(Reset), .KB_Status(keyboard_1_avail), .in_2(keyboard_1_data),
    .KB_Clock(ioshim_1_kb_clock), .KB_Clear(ioshim_1_kb_clear), .out_12(ioshim_1_out_12), .TTY_Ready(in_22),
    .out_13(ioshim_1_out_13), .TTY_Enable(ioshim_1_tty_enable), .TTY_Clear(ioshim_1_tty_clear));
  assign ioshim_1_out_12 = kbyte_buddy_1_sel ? rom_3_data : 8'bz;  // Controlled_Buffer controlled_buffer_4
  ROM #(.addrWidth(10)) rom_3 (.addr(kbyte_buddy_1_ram_addr), .data(rom_3_data), .sel(kbyte_buddy_1_sel));
  RAM #(.addrWidth(10), .bus("separate")) ram_1 (
    .addr(kbyte_buddy_2_ram_addr), .din(D_Data_to_RAM), .data(ram_1_data), .str(D_RAMWrite),
    .sel(kbyte_buddy_2_sel), .clk(out_23), .ld(or_3_out), .clr(Reset));
  assign ioshim_1_out_12 = kbyte_buddy_2_sel ? ram_1_data : 8'bz;  // Controlled_Buffer controlled_buffer_5
  and and_2 (Exception, or_2_out, PrivMode, comparator_2_eq);
  TTY tty_1 (.data(ioshim_1_out_13), .clk(out_23), .we(ioshim_1_tty_enable), .clr(ioshim_1_tty_clear));
  Keyboard keyboard_1 (
    .clk(ioshim_1_kb_clock), .re(1'b1), .clr(ioshim_1_kb_clear), .avail(keyboard_1_avail),
    .data(keyboard_1_data));
  assign I_Data_from_RAM = I_RAMread ? ioshim_1_out_12 : 8'bz;  // Controlled_Buffer controlled_buffer_6
  assign D_Data_from_RAM = D_RAMread ? ioshim_1_out_12 : 8'bz;  // Controlled_Buffer controlled_buffer_7

  // Other names for the same wires on the sheet: ldPC = in_11; newPCsel[1:0] = in_7; DMemWrite = in_3; DMemReq = in_1;
  //   ldMDR = in_9; MDRsel = in_5; ldMAR = in_16; MARsel = in_14; ldCC = in_2; aluOPsel = _0_add; aluBsel = in_13;
  //   aluAsel[1:0] = in_8; dstMreq = in_15; dstEreq[1:0] = in_10; dstEsel = in_6; srcBsel = rB____F; srcAsel = in_18;
  //   valCsel = in_19; PCIncSel[1:0] = in_4; IMemReq = in_12; Clock = out_23

  // Notes on the sheet:
  //   Y86 Processor
  //   March 5, 2018
  //   connect to memory!
  //   Fetch
  //   valP
  //   valM
  //   IR[1:4]
  //   IR[2:5]
  //   Decode/Write-Back
  //   Execute
  //   contents of rom_1 (hex, n*v repeats v):
  //   80000041 c0 1843 80 1045 86 400040 1048 89 540 39*0 140 21080140 71180140 7010a142 70108144 20860140
  //   40000740 46b0e342 ea18047 26b0a142 2ea18144 70960140 6b0e142 140 6b0e342
  //   Completed by Graham Hazlett, from skeleton by SWS and Taylor Cathcart and Vijay Kothari, based on a skeleton from Matt Kretchmar
  //   contents of rom_2 (hex, n*v repeats v):
  //   61*0 a c a
  //   Memory
  //   PC
  //   Priviledge
  //   connect to memory (and io,
  //    pretending to be memory)
  //   Exception
  //   contents of rom_3 (hex, n*v repeats v):
  //   e0 30 f4 30 4 0 0 70 0 3 246*0 50 3f 0 fe ff 0 60 33 73 0 1 0 0 50 f 4 fe ff 0 e0 90 235*0 50 1f 8
  //   fe ff 0 60 11 73 0 2 0 0 30 f0 45 0 0 0 40 f c fe ff 0 30 f0 72 0 0 0 40 f c fe ff 0 30 f0 72 0 0 0
  //   40 f c fe ff 0 30 f0 6f 0 0 0 40 f c fe ff 0 30 f0 72 0 0 0 40 f c fe ff 0 30 f0 21 0 0 0 40 f c fe
  //   ff 172*0 d0 50 3f 0 fe ff 0 60 33 73 1 3 0 0 50 f 4 fe ff
endmodule

module isplit (
  input  [7:0] B0,
  input  [7:0] B1,
  input  [7:0] B2,
  input  [7:0] B3,
  input  [7:0] B4,
  input  [7:0] B5,
  output [3:0] icode,
  output [3:0] ifun,
  output [3:0] rA,
  output [3:0] rB,
  output [31:0] Dest,
  output [31:0] D_V
);


  assign D_V = {B5, B4, B3, B2};
  assign Dest = {B4, B3, B2, B1};
  assign icode = B0[7:4];
  assign ifun = B0[3:0];
  assign rA = B1[7:4];
  assign rB = B1[3:0];
endmodule

module regreader (
  input  [2:0] srcA,
  input  [2:0] srcB,
  input  [31:0] Q,
  input  [31:0] Q_2,
  input  [31:0] Q_3,
  input  reset,
  input  [31:0] Q_4,
  input  [31:0] Q_5,
  input  [31:0] Q_6,
  input  [31:0] Q_7,
  input  [31:0] Q_8,
  output CLR,
  output [31:0] valA,
  output [31:0] valB,
  output CLR_2,
  output CLR_3,
  output CLR_4,
  output CLR_5,
  output CLR_6,
  output CLR_7,
  output CLR_8
);

  Multiplexer #(.select(3), .width(32), .enable("false")) multiplexer_1 (
    .in0(Q), .in1(Q_2), .in2(Q_3), .in3(Q_4), .in4(Q_5), .in5(Q_6), .in6(Q_7), .in7(Q_8), .out(valA),
    .sel(srcA));
  Multiplexer #(.select(3), .width(32), .enable("false")) multiplexer_2 (
    .in0(Q), .in1(Q_2), .in2(Q_3), .in3(Q_4), .in4(Q_5), .in5(Q_6), .in6(Q_7), .in7(Q_8), .out(valB),
    .sel(srcB));

  assign CLR = reset;
  assign CLR_2 = reset;
  assign CLR_3 = reset;
  assign CLR_4 = reset;
  assign CLR_5 = reset;
  assign CLR_6 = reset;
  assign CLR_7 = reset;
  assign CLR_8 = reset;
endmodule

module regwriter (
  input  [2:0] dstE,
  input  reqE,
  input  [2:0] dstM,
  input  reqM,
  input  [31:0] valE,
  input  [31:0] valM,
  output [31:0] D0,
  output EN,
  output [31:0] D1,
  output EN_2,
  output [31:0] D2,
  output EN_3,
  output [31:0] D3,
  output EN_4,
  output [31:0] D4,
  output EN_5,
  output [31:0] D5,
  output EN_6,
  output [31:0] D6,
  output EN_7,
  output [31:0] D7,
  output EN_8
);

  wire [1:0] demultiplexer_3_out0, demultiplexer_3_out1, demultiplexer_3_out2, demultiplexer_3_out3,
       demultiplexer_3_out4, demultiplexer_3_out5, demultiplexer_3_out6, demultiplexer_3_out7;
  wire [31:0] demultiplexer_1_out0, demultiplexer_1_out1, demultiplexer_1_out2, demultiplexer_1_out3,
       demultiplexer_1_out4, demultiplexer_1_out5, demultiplexer_1_out6, demultiplexer_1_out7,
       demultiplexer_2_out0, demultiplexer_2_out1, demultiplexer_2_out2, demultiplexer_2_out3,
       demultiplexer_2_out4, demultiplexer_2_out5, demultiplexer_2_out6, demultiplexer_2_out7;

  Demultiplexer #(.select(3), .width(32)) demultiplexer_1 (
    .out0(demultiplexer_1_out0), .out1(demultiplexer_1_out1), .out2(demultiplexer_1_out2),
    .out3(demultiplexer_1_out3), .out4(demultiplexer_1_out4), .out5(demultiplexer_1_out5),
    .out6(demultiplexer_1_out6), .out7(demultiplexer_1_out7), .in(valE), .sel(dstE));  // open: en
  Demultiplexer #(.select(3), .width(32)) demultiplexer_2 (
    .out0(demultiplexer_2_out0), .out1(demultiplexer_2_out1), .out2(demultiplexer_2_out2),
    .out3(demultiplexer_2_out3), .out4(demultiplexer_2_out4), .out5(demultiplexer_2_out5),
    .out6(demultiplexer_2_out6), .out7(demultiplexer_2_out7), .in(valM), .sel(dstM));  // open: en
  Demultiplexer #(.select(3)) demultiplexer_3 (
    .out0(demultiplexer_3_out0[0]), .out1(demultiplexer_3_out1[0]), .out2(demultiplexer_3_out2[0]),
    .out3(demultiplexer_3_out3[0]), .out4(demultiplexer_3_out4[0]), .out5(demultiplexer_3_out5[0]),
    .out6(demultiplexer_3_out6[0]), .out7(demultiplexer_3_out7[0]), .in(reqE), .sel(dstE));  // open: en
  Demultiplexer #(.select(3)) demultiplexer_4 (
    .out0(demultiplexer_3_out0[1]), .out1(demultiplexer_3_out1[1]), .out2(demultiplexer_3_out2[1]),
    .out3(demultiplexer_3_out3[1]), .out4(demultiplexer_3_out4[1]), .out5(demultiplexer_3_out5[1]),
    .out6(demultiplexer_3_out6[1]), .out7(demultiplexer_3_out7[1]), .in(reqM), .sel(dstM));  // open: en
  Multiplexer #(.select(2), .width(32), .enable("false")) multiplexer_1 (
    .in1(demultiplexer_1_out0), .in2(demultiplexer_2_out0), .out(D0), .sel(demultiplexer_3_out0));  // open: in0, in3
  Multiplexer #(.select(2), .width(32), .enable("false")) multiplexer_2 (
    .in1(demultiplexer_1_out1), .in2(demultiplexer_2_out1), .out(D1), .sel(demultiplexer_3_out1));  // open: in0, in3
  Multiplexer #(.select(2), .width(32), .enable("false")) multiplexer_3 (
    .in1(demultiplexer_1_out2), .in2(demultiplexer_2_out2), .out(D2), .sel(demultiplexer_3_out2));  // open: in0, in3
  Multiplexer #(.select(2), .width(32), .enable("false")) multiplexer_4 (
    .in1(demultiplexer_1_out3), .in2(demultiplexer_2_out3), .out(D3), .sel(demultiplexer_3_out3));  // open: in0, in3
  Multiplexer #(.select(2), .width(32), .enable("false")) multiplexer_5 (
    .in1(demultiplexer_1_out4), .in2(demultiplexer_2_out4), .out(D4), .sel(demultiplexer_3_out4));  // open: in0, in3
  Multiplexer #(.select(2), .width(32), .enable("false")) multiplexer_6 (
    .in1(demultiplexer_1_out5), .in2(demultiplexer_2_out5), .out(D5), .sel(demultiplexer_3_out5));  // open: in0, in3
  Multiplexer #(.select(2), .width(32), .enable("false")) multiplexer_7 (
    .in1(demultiplexer_1_out6), .in2(demultiplexer_2_out6), .out(D6), .sel(demultiplexer_3_out6));  // open: in0, in3
  Multiplexer #(.select(2), .width(32), .enable("false")) multiplexer_8 (
    .in1(demultiplexer_1_out7), .in2(demultiplexer_2_out7), .out(D7), .sel(demultiplexer_3_out7));  // open: in0, in3
  xor xor_1 (EN, demultiplexer_3_out0[0], demultiplexer_3_out0[1]);
  xor xor_2 (EN_2, demultiplexer_3_out1[0], demultiplexer_3_out1[1]);
  xor xor_3 (EN_3, demultiplexer_3_out2[0], demultiplexer_3_out2[1]);
  xor xor_4 (EN_4, demultiplexer_3_out3[0], demultiplexer_3_out3[1]);
  xor xor_5 (EN_5, demultiplexer_3_out4[0], demultiplexer_3_out4[1]);
  xor xor_6 (EN_6, demultiplexer_3_out5[0], demultiplexer_3_out5[1]);
  xor xor_7 (EN_7, demultiplexer_3_out6[0], demultiplexer_3_out6[1]);
  xor xor_8 (EN_8, demultiplexer_3_out7[0], demultiplexer_3_out7[1]);
endmodule

module alu (
  input  [31:0] ALU_A,
  input  [31:0] ALU_B,
  input  [3:0] ALU_op,
  output [2:0] CC,
  output [31:0] valE
);

  wire and_1_out, and_2_out, and_3_out, and_4_out, multiplexer_1_out, multiplexer_2_out, not_1_out,
       not_2_out, or_1_out;
  wire [31:0] adder_1_out, and_5_out, subtractor_1_out, xor_1_out;

  Multiplexer multiplexer_1 (.in0(ALU_A[31]), .in1(not_1_out), .out(multiplexer_1_out), .sel(ALU_op[0]));  // open: en
  not not_1 (not_1_out, ALU_A[31]);
  Multiplexer multiplexer_2 (.in0(ALU_A[31]), .in1(not_2_out), .out(multiplexer_2_out), .sel(ALU_op[0]));  // open: en
  not not_2 (not_2_out, ALU_A[31]);
  and and_1 (and_1_out, multiplexer_1_out, ALU_B[31]);
  and and_2 (and_2_out, ~multiplexer_2_out, ~ALU_B[31]);  // AND_Gate
  and and_3 (and_3_out, and_1_out, ~CC[1]);  // AND_Gate
  and and_4 (and_4_out, CC[1], and_2_out);
  or or_1 (or_1_out, and_3_out, and_4_out);
  Adder #(.width(32)) adder_1 (.a(ALU_B), .b(ALU_A), .out(adder_1_out));  // open: cin, cout
  Subtractor #(.width(32)) subtractor_1 (.a(ALU_B), .b(ALU_A), .out(subtractor_1_out));  // open: bin, bout
  assign and_5_out = ALU_B & ALU_A;  // AND_Gate and_5, 32 bits wide
  assign xor_1_out = ALU_B ^ ALU_A;  // XOR_Gate xor_1, 32 bits wide
  Multiplexer multiplexer_3 (.in0(or_1_out), .in1(1'b0), .out(CC[0]), .sel(ALU_op[1]));  // open: en
  Multiplexer #(.select(2), .width(32)) multiplexer_4 (
    .in0(adder_1_out), .in1(subtractor_1_out), .in2(and_5_out), .in3(xor_1_out), .out({CC[1], valE[30:0]}),
    .sel(ALU_op[1:0]));  // open: en
  Comparator #(.width(32), .mode("unsigned")) comparator_1 (
    .a({32{1'b0}}), .b({CC[1], valE[30:0]}), .eq(CC[2]));  // open: gt, lt

  assign valE[31] = CC[1];

  // Notes on the sheet:
  //   determine overflow flag:
  //   addl [00]
  //   subl [01]
  //   xorl [11]
  //   Determine overflow only for addl and subl
  //   determine if negative (if most significant bit high)
  //   determine if equal to zero
  //   (Zero Bit, Signed Bit, Overflow Bit)
endmodule

module MSB (
  input  [31:0] Value,
  output MSB
);


  assign MSB = Value[31];
endmodule

module CND (
  input  [2:0] ZSO,
  input  [3:0] ifun,
  output CND
);

  wire and_1_out, not_1_out, not_2_out, or_1_out, xor_1_out;

  xor xor_1 (xor_1_out, ZSO[1], ZSO[0]);
  not not_1 (not_1_out, xor_1_out);
  or or_1 (or_1_out, ZSO[2], xor_1_out);
  not not_2 (not_2_out, ZSO[2]);
  and and_1 (and_1_out, not_2_out, not_1_out);
  Multiplexer #(.select(4)) multiplexer_1 (
    .in0(1'b1), .in1(or_1_out), .in2(xor_1_out), .in3(ZSO[2]), .in4(not_2_out), .in5(not_1_out),
    .in6(and_1_out), .in7(1'b0), .in8(1'b0), .in9(1'b0), .in10(1'b0), .in11(1'b0), .in12(1'b0), .in13(1'b0),
    .in14(1'b0), .in15(1'b0), .out(CND), .sel(ifun));  // open: en

  // Notes on the sheet:
  //   Sample CND, from SWS
endmodule

module ishim (
  input  req,
  input  [31:0] in_2,
  input  reset,
  input  clock,
  input  [7:0] in_5,
  output [7:0] out_6,
  output [7:0] out_7,
  output [7:0] out_8,
  output [7:0] out_9,
  output [7:0] out_10,
  output [7:0] out_11,
  output done,
  output RAMuse,
  output [31:0] out_14,
  output RAMread
);

  wire decoder_1_out0, decoder_1_out1, decoder_1_out2, decoder_1_out3, decoder_1_out4, decoder_1_out5,
       decoder_1_out6, or_1_out;
  wire [2:0] _3bit_q;
  wire [31:0] adder_1_out, bit_extender_1_out;

  D_Flip_Flop d_ff_1 (.clk(clock), .D(req), .Q(RAMread), .Qn(done), .preset(1'b0), .en(done), .reset(or_1_out));
  Decoder #(.select(3), .disabled(0)) decoder_1 (
    .out0(decoder_1_out0), .out1(decoder_1_out1), .out2(decoder_1_out2), .out3(decoder_1_out3),
    .out4(decoder_1_out4), .out5(decoder_1_out5), .out6(decoder_1_out6), .sel(_3bit_q), .en(RAMread));  // open: out7
  Counter #(.width(3), .max('h7)) _3bit (
    .load(1'b0), .count(RAMread), .Q(_3bit_q), .clk(clock), .clr(or_1_out));  // open: D, carry
  or or_1 (or_1_out, decoder_1_out6, reset);
  assign bit_extender_1_out = {{29{1'b0}}, _3bit_q};  // Bit_Extender bit_extender_1
  Adder #(.width(32)) adder_1 (.a(in_2), .b(bit_extender_1_out), .out(adder_1_out), .cin(1'b0));  // open: cout
  alu alu_1 ();  // open: ALU_A, CC, ALU_B, valE, ALU_op
  assign out_14 = RAMread ? adder_1_out : 32'bz;  // Controlled_Buffer controlled_buffer_1
  Register #(.trigger("falling")) register_1 (.D(in_5), .en(decoder_1_out0), .Q(out_6), .clk(clock), .clr(reset));
  Register #(.trigger("falling")) register_2 (.D(in_5), .en(decoder_1_out1), .Q(out_7), .clk(clock), .clr(reset));
  Register #(.trigger("falling")) register_3 (.D(in_5), .en(decoder_1_out2), .Q(out_8), .clk(clock), .clr(reset));
  Register #(.trigger("falling")) register_4 (.D(in_5), .en(decoder_1_out3), .Q(out_9), .clk(clock), .clr(reset));
  Register #(.trigger("falling")) register_5 (.D(in_5), .en(decoder_1_out4), .Q(out_10), .clk(clock), .clr(reset));
  Register #(.trigger("falling")) register_6 (.D(in_5), .en(decoder_1_out5), .Q(out_11), .clk(clock), .clr(reset));

  assign RAMuse = RAMread;

  // Notes on the sheet:
  //   addr
  //   in use?
  //   state
  //   RAMaddr (32 bits)
  //   data from RAM (8 bits)
  //   byte 0
  //   byte 1
  //   byte 2
  //   byte 3
  //   byte 4
  //   byte 5
endmodule

module dhsim (
  input  [31:0] in_1,
  input  [7:0] in_2,
  input  [31:0] in_3,
  input  DMem_Write,
  input  req,
  input  reset,
  input  clock,
  output [31:0] DataOut,
  output [7:0] out_9,
  output RAMwrite,
  output RAMread,
  output done,
  output RAMuse,
  output [31:0] out_14
);

  wire comparator_1_eq, d_ff_1_q, d_ff_1_qn, decoder_1_out0, decoder_1_out1, decoder_1_out2, decoder_1_out3,
       or_1_out;
  wire [1:0] bit_extender_2_out;
  wire [2:0] _3bit_q;
  wire [31:0] adder_1_out, bit_extender_1_out;

  assign bit_extender_1_out = {{29{1'b0}}, _3bit_q};  // Bit_Extender bit_extender_1
  D_Flip_Flop d_ff_1 (
    .clk(clock), .D(DMem_Write), .Q(d_ff_1_q), .Qn(d_ff_1_qn), .preset(1'b0), .en(done), .reset(reset));
  D_Flip_Flop in_use (.clk(clock), .D(req), .Q(RAMuse), .Qn(done), .preset(1'b0), .en(done), .reset(or_1_out));
  Adder #(.width(32)) adder_1 (.a(in_1), .b(bit_extender_1_out), .out(adder_1_out), .cin(1'b0));  // open: cout
  and and_1 (RAMwrite, RAMuse, d_ff_1_q);
  and and_2 (RAMread, d_ff_1_qn, RAMuse);
  Decoder #(.select(3), .disabled(0)) decoder_1 (
    .out0(decoder_1_out0), .out1(decoder_1_out1), .out2(decoder_1_out2), .out3(decoder_1_out3),
    .sel(_3bit_q), .en(RAMread));  // open: out4, out5, out6, out7
  Counter #(.width(3), .max('h7)) _3bit (
    .load(1'b0), .count(RAMuse), .Q(_3bit_q), .clk(clock), .clr(or_1_out));  // open: D, carry
  or or_1 (or_1_out, comparator_1_eq, reset);
  Comparator #(.width(3)) comparator_1 (.a(_3bit_q), .b(3'b100), .eq(comparator_1_eq));  // open: gt, lt
  assign out_14 = RAMuse ? adder_1_out : 32'bz;  // Controlled_Buffer controlled_buffer_1
  Bit_Extender #(.in_width(3), .out_width(2)) bit_extender_2 (.in(_3bit_q), .out(bit_extender_2_out));
  Multiplexer #(.select(2), .width(8)) multiplexer_1 (
    .in0(in_3[7:0]), .in1(in_3[15:8]), .in2(in_3[23:16]), .in3(in_3[31:24]), .out(out_9),
    .sel(bit_extender_2_out), .en(RAMwrite));
  Register #(.trigger("falling")) register_1 (
    .D(in_2), .en(decoder_1_out0), .Q(DataOut[7:0]), .clk(clock), .clr(reset));
  Register #(.trigger("falling")) register_2 (
    .D(in_2), .en(decoder_1_out1), .Q(DataOut[15:8]), .clk(clock), .clr(reset));
  Register #(.trigger("falling")) register_3 (
    .D(in_2), .en(decoder_1_out2), .Q(DataOut[23:16]), .clk(clock), .clr(reset));
  Register #(.trigger("falling")) register_4 (
    .D(in_2), .en(decoder_1_out3), .Q(DataOut[31:24]), .clk(clock), .clr(reset));

  // Notes on the sheet:
  //   address
  //   writing?
  //   reading?
  //   state
  //   data in
  //   RAMaddr (32 bits)
  //   data from RAM (8 bits)
  //   data to RAM (8 bits)
endmodule

module kbyte_buddy (
  input  [31:0] addr,
  input  [31:0] addr_prefix,
  input  \use ,
  output [9:0] ram_addr,
  output sel
);

  wire comparator_1_eq;
  wire [31:0] and_1_out;

  Bit_Extender #(.in_width(32), .out_width(10)) bit_extender_1 (.in(addr), .out(ram_addr));
  assign and_1_out = addr & 32'hfffffc00;  // AND_Gate and_1, 32 bits wide
  Comparator #(.width(32)) comparator_1 (.a(and_1_out), .b(addr_prefix), .eq(comparator_1_eq));  // open: gt, lt
  and and_2 (sel, comparator_1_eq, \use );
endmodule

module ioshim (
  input  KB_Status,
  input  [6:0] in_2,
  input  RAM_Use,
  input  [31:0] in_4,
  input  [7:0] in_5,
  input  RAM_Read,
  input  RAM_Write,
  input  TTY_Ready,
  input  reset,
  output KB_Clock,
  output KB_Clear,
  output [7:0] out_12,
  output [6:0] out_13,
  output TTY_Enable,
  output TTY_Clear
);

  wire and_1_out, and_2_out, comparator_1_eq, comparator_2_eq, comparator_3_eq, comparator_4_eq,
       comparator_5_eq, nor_1_out;
  wire [7:0] bit_extender_1_out, bit_extender_2_out, bit_extender_3_out, controlled_buffer_1_out,
       controlled_buffer_6_out, register_1_q;

  Comparator #(.width(32)) comparator_1 (.a(32'hfffe00), .b(in_4), .eq(comparator_1_eq));  // open: gt, lt
  and and_1 (and_1_out, RAM_Use, RAM_Read);
  and and_2 (and_2_out, RAM_Use, RAM_Write);
  Comparator #(.width(32)) comparator_2 (.a(32'hfffe04), .b(in_4), .eq(comparator_2_eq));  // open: gt, lt
  Comparator #(.width(32)) comparator_3 (.a(32'hfffe08), .b(in_4), .eq(comparator_3_eq));  // open: gt, lt
  Comparator #(.width(32)) comparator_4 (.a(32'hfffe0c), .b(in_4), .eq(comparator_4_eq));  // open: gt, lt
  assign bit_extender_1_out = {{1{1'b0}}, in_2};  // Bit_Extender bit_extender_1
  assign controlled_buffer_1_out = nor_1_out ? {8{1'b0}} : 8'bz;  // Controlled_Buffer controlled_buffer_1
  nor nor_1 (nor_1_out, comparator_1_eq, comparator_2_eq, comparator_3_eq, comparator_4_eq);
  and and_3 (TTY_Enable, comparator_4_eq, and_2_out);
  Register register_1 (.D(bit_extender_1_out), .Q(register_1_q), .clk(KB_Clock));  // open: en, clr
  assign controlled_buffer_1_out = comparator_1_eq ? bit_extender_2_out : 8'bz;  // Controlled_Buffer controlled_buffer_2
  assign bit_extender_2_out = {{7{1'b0}}, KB_Status};  // Bit_Extender bit_extender_2
  assign controlled_buffer_1_out = comparator_2_eq ? register_1_q : 8'bz;  // Controlled_Buffer controlled_buffer_3
  assign bit_extender_3_out = {{7{1'b0}}, TTY_Ready};  // Bit_Extender bit_extender_3
  Bit_Extender #(.out_width(7)) bit_extender_4 (.in(in_5), .out(out_13));
  and and_4 (KB_Clock, comparator_2_eq, and_1_out);
  assign controlled_buffer_1_out = comparator_3_eq ? bit_extender_3_out : 8'bz;  // Controlled_Buffer controlled_buffer_4
  Comparator #(.width(24)) comparator_5 (.a(24'hfffe), .b(in_4[31:8]), .eq(comparator_5_eq));  // open: gt, lt
  assign out_12 = comparator_5_eq ? controlled_buffer_6_out : 8'bz;  // Controlled_Buffer controlled_buffer_5
  assign controlled_buffer_6_out = and_1_out ? controlled_buffer_1_out : 8'bz;  // Controlled_Buffer controlled_buffer_6

  assign KB_Clear = reset;
  assign TTY_Clear = reset;

  // Notes on the sheet:
  //   RAM Address
  //   Incoming Data
  //   KB Data
  //   Outgoing Data
  //   TTY Data
endmodule

module useq (
  input  [5:0] CurrentState,
  input  [1:0] Select,
  input  [3:0] icode,
  input  [5:0] valN,
  input  DMemDone,
  input  IMemDone,
  input  Exception,
  output [5:0] NextState
);

  wire [5:0] bit_extender_1_out, multiplexer_1_out, multiplexer_2_out, multiplexer_3_out;

  assign bit_extender_1_out = {{2{1'b1}}, icode};  // Bit_Extender bit_extender_1
  Multiplexer #(.width(6)) multiplexer_1 (
    .in0(CurrentState), .in1(valN), .out(multiplexer_1_out), .sel(DMemDone));  // open: en
  Multiplexer #(.width(6)) multiplexer_2 (
    .in0(CurrentState), .in1(bit_extender_1_out), .out(multiplexer_2_out), .sel(IMemDone));  // open: en
  Multiplexer #(.select(2), .width(6)) multiplexer_3 (
    .in0(CurrentState), .in1(valN), .in2(multiplexer_1_out), .in3(multiplexer_2_out),
    .out(multiplexer_3_out), .sel(Select));  // open: en
  Multiplexer #(.width(6)) multiplexer_4 (
    .in0(multiplexer_3_out), .in1({6{1'b1}}), .out(NextState), .sel(Exception));  // open: en
endmodule
