// Logisim project HW1Q2.circ as structural Verilog: 2 circuits, main circuit main
module main (
  input  in_1,
  input  in_2,
  output out_3
);

  \xor  xor_1 (.in_1(in_1), .in_2(in_2), .out_3(out_3));
endmodule

module \xor  (
  input  in_1,
  input  in_2,
  output out_3
);

  wire transistor_2_out, transistor_3_out, transistor_5_out, transistor_8_out;

  Transistor #(.\type ("n")) transistor_1 (.in(transistor_2_out), .out(out_3), .gate(in_1));
  Transistor transistor_2 (.in(1'b1), .out(transistor_2_out), .gate(in_2));
  Transistor #(.\type ("n")) transistor_3 (.in(1'b1), .out(transistor_3_out), .gate(in_2));
  Transistor transistor_4 (.in(transistor_3_out), .out(out_3), .gate(in_1));
  Transistor #(.\type ("n")) transistor_5 (.in(1'b0), .out(transistor_5_out), .gate(in_2));
  Transistor #(.\type ("n")) transistor_6 (.in(transistor_5_out), .out(out_3), .gate(in_1));
  Transistor transistor_7 (.in(transistor_8_out), .out(out_3), .gate(in_1));
  Transistor transistor_8 (.in(1'b0), .out(transistor_8_out), .gate(in_2));
endmodule
