// Logisim project skeleton.circ as structural Verilog: 1 circuit, main circuit main
module main (
  input  In0,
  input  In1,
  input  In2,
  input  In3,
  output Out
);

  wire nor_1_out, nor_2_out, nor_3_out, xor_1_out, xor_2_out, xor_3_out;

  nor nor_1 (nor_1_out, In0, In1);
  xor xor_1 (xor_1_out, In0, In1);
  xor xor_2 (xor_2_out, In2, In3);
  nor nor_2 (nor_2_out, In2, In3);
  xor xor_3 (xor_3_out, xor_1_out, xor_2_out);
  and and_1 (Out, xor_3_out, nor_3_out);
  nor nor_3 (nor_3_out, nor_1_out, nor_2_out);
endmodule
