// Logisim project HW2Q3.circ as structural Verilog: 1 circuit, main circuit main
module main (
  input  [3:0] A,
  input  [3:0] B,
  output A___B
);

  wire and_1_out, and_2_out, and_3_out, and_4_out, and_5_out, and_6_out, and_7_out, or_1_out, or_2_out,
       xnor_1_out, xnor_2_out, xnor_3_out, xor_1_out, xor_2_out, xor_3_out, xor_4_out;

  Hex_Digit_Display hex_digit_display_1 (.value(A));  // open: dp
  Hex_Digit_Display hex_digit_display_2 (.value(B));  // open: dp
  xor xor_1 (xor_1_out, A[2], B[2]);
  xor xor_2 (xor_2_out, A[3], B[3]);
  and and_1 (and_1_out, A[0], xor_3_out);
  xor xor_3 (xor_3_out, A[0], B[0]);
  xnor xnor_1 (xnor_1_out, A[1], B[1]);
  and and_2 (and_2_out, A[1], xor_4_out);
  xor xor_4 (xor_4_out, A[1], B[1]);
  xnor xnor_2 (xnor_2_out, A[2], B[2]);
  and and_3 (and_3_out, A[2], xor_1_out);
  xnor xnor_3 (xnor_3_out, B[3], A[3]);
  and and_4 (and_4_out, A[3], xor_2_out);
  and and_5 (and_5_out, and_1_out, xnor_1_out);
  or or_1 (or_1_out, and_5_out, and_2_out);
  and and_6 (and_6_out, or_1_out, xnor_2_out);
  or or_2 (or_2_out, and_6_out, and_3_out);
  and and_7 (and_7_out, or_2_out, xnor_3_out);
  or or_3 (A___B, and_7_out, and_4_out);
endmodule
