// Logisim project HW2Q4.circ as structural Verilog: 1 circuit, main circuit main
module main (
  input  [3:0] Ones,
  input  [3:0] Tens,
  input  [3:0] Hundreds,
  input  [3:0] Thousands,
  output [5:0] Sum_of_all_digits,
  output NotBCD,
  output SixMult
);

  wire _5_bit_multiples_of_3_out, and_1_out, combine_with_multiples_of_2_out, comparator_1_lt,
       comparator_2_lt, comparator_3_lt, comparator_4_lt, decoder_1_out1, decoder_1_out3, decoder_1_out4,
       decoder_1_out6, decoder_1_out9, decoder_1_out12, decoder_1_out15, decoder_1_out18, decoder_1_out21,
       decoder_1_out24, decoder_1_out27, decoder_1_out30, not_1_out, or_1_out, Plus__33__and__36__cases_out;
  wire [3:0] adder_1_out;
  wire [4:0] adder_2_out;
  wire [4:4] adder_1_cout;
  wire [5:5] adder_2_cout;

  Hex_Digit_Display hex_digit_display_1 (.value(Thousands));  // open: dp
  Hex_Digit_Display hex_digit_display_2 (.value(Hundreds));  // open: dp
  Hex_Digit_Display hex_digit_display_3 (.value(Tens));  // open: dp
  Comparator #(.width(4), .mode("unsigned")) comparator_1 (
    .a(Ones), .b(4'b1010), .lt(comparator_1_lt));  // open: gt, eq
  Comparator #(.width(4), .mode("unsigned")) comparator_2 (
    .a(Tens), .b(4'b1010), .lt(comparator_2_lt));  // open: gt, eq
  Comparator #(.width(4), .mode("unsigned")) comparator_3 (
    .a(Hundreds), .b(4'b1010), .lt(comparator_3_lt));  // open: gt, eq
  Comparator #(.width(4), .mode("unsigned")) comparator_4 (
    .a(Thousands), .b(4'b1010), .lt(comparator_4_lt));  // open: gt, eq
  Hex_Digit_Display hex_digit_display_4 (.value(Ones));  // open: dp
  Adder #(.width(4)) adder_1 (.a(Ones), .b(Tens), .out(adder_1_out), .cout(adder_1_cout[4]));  // open: cin
  nand nand_1 (NotBCD, comparator_1_lt, comparator_2_lt, comparator_3_lt, comparator_4_lt);
  Adder #(.width(5)) adder_2 (
    .a({adder_1_cout[4], adder_1_out}), .b({1'b0, Hundreds}), .out(adder_2_out), .cout(adder_2_cout[5]));  // open: cin
  Adder #(.width(6)) adder_3 (
    .a({adder_2_cout[5], adder_2_out}), .b({2'b00, Thousands}), .out(Sum_of_all_digits));  // open: cin, cout
  Decoder #(.select(5)) decoder_1 (
    .out1(decoder_1_out1), .out3(decoder_1_out3), .out4(decoder_1_out4), .out6(decoder_1_out6),
    .out9(decoder_1_out9), .out12(decoder_1_out12), .out15(decoder_1_out15), .out18(decoder_1_out18),
    .out21(decoder_1_out21), .out24(decoder_1_out24), .out27(decoder_1_out27), .out30(decoder_1_out30),
    .sel(Sum_of_all_digits[4:0]));  // open: out0, out2, out5, out7, out8, out10, out11, out13, out14, out16, out17, out19, out20, out22, out23, out25, out26, out28, out29, out31, en
  or _5_bit_multiples_of_3 (_5_bit_multiples_of_3_out, decoder_1_out3, decoder_1_out6, decoder_1_out9, decoder_1_out12, decoder_1_out15, decoder_1_out18, decoder_1_out21, decoder_1_out24, decoder_1_out27, decoder_1_out30);
  or or_1 (or_1_out, decoder_1_out1, decoder_1_out4);
  and and_1 (and_1_out, or_1_out, Sum_of_all_digits[5]);
  or Plus__33__and__36__cases (Plus__33__and__36__cases_out, _5_bit_multiples_of_3_out, and_1_out);
  and combine_with_multiples_of_2 (combine_with_multiples_of_2_out, Plus__33__and__36__cases_out, ~Ones[0]);  // AND_Gate
  and check_for_BCD_input (SixMult, combine_with_multiples_of_2_out, not_1_out);
  not not_1 (not_1_out, NotBCD);
endmodule
