// Logisim project HW3Q2.circ as structural Verilog: 1 circuit, main circuit main
module main (
  input  [3:0] most_significant_nibble_of_8_bit_address,
  input  [3:0] least_significant_nibble_of_8_bit_address,
  input  [7:0] data_in__8_bits,
  input  write__rising_edge,
  output [3:0] out_5
);

  wire comparator_1_eq, comparator_2_eq;
  wire [7:0] controlled_buffer_2_out, ram_1_data;

  Comparator #(.width(4), .mode("unsigned")) comparator_1 (
    .a(4'b1111), .b(most_significant_nibble_of_8_bit_address), .eq(comparator_1_eq));  // open: gt, lt
  assign out_5 = comparator_1_eq ? least_significant_nibble_of_8_bit_address : 4'bz;  // Controlled_Buffer controlled_buffer_1
  RAM #(.addrWidth(4), .bus("separate")) ram_1 (
    .addr(out_5), .din(data_in__8_bits), .data(ram_1_data), .clk(write__rising_edge));  // open: str, sel, ld, clr
  Comparator #(.width(4), .mode("unsigned")) comparator_2 (
    .a(4'b1111), .b(most_significant_nibble_of_8_bit_address), .eq(comparator_2_eq));  // open: gt, lt
  assign controlled_buffer_2_out = comparator_2_eq ? ram_1_data : 8'bz;  // Controlled_Buffer controlled_buffer_2
  // Probe on controlled_buffer_2_out

  // Notes on the sheet:
  //   arbitrary 4-bit constant "Y"
endmodule
