// Logisim project HW3Q3.circ as structural Verilog: 3 circuits, main circuit regwriter
module hw3 (
  input  [31:0] valE,
  input  [31:0] valM,
  input  [2:0] dstE,
  input  reqE,
  input  [2:0] dstM,
  input  reqM,
  input  clock,
  input  [2:0] srcA,
  input  [2:0] srcB,
  input  clr,
  output [31:0] valA,
  output [31:0] valB
);

  wire regreader_1_clr, regreader_1_clr_2, regreader_1_clr_3, regreader_1_clr_4, regreader_1_clr_5,
       regreader_1_clr_6, regreader_1_clr_7, regreader_1_clr_8, regwriter_1_en, regwriter_1_en_2,
       regwriter_1_en_3, regwriter_1_en_4, regwriter_1_en_5, regwriter_1_en_6, regwriter_1_en_7,
       regwriter_1_en_8;
  wire [31:0] register_1_q, register_2_q, register_3_q, register_4_q, register_5_q, register_6_q,
       register_7_q, register_8_q, regwriter_1_d0, regwriter_1_d1, regwriter_1_d2, regwriter_1_d3,
       regwriter_1_d4, regwriter_1_d5, regwriter_1_d6, regwriter_1_d7;

  regwriter regwriter_1 (
    .dstE(dstE), .reqE(reqE), .dstM(dstM), .reqM(reqM), .valE(valE), .valM(valM), .D0(regwriter_1_d0),
    .EN(regwriter_1_en), .D1(regwriter_1_d1), .EN_2(regwriter_1_en_2), .D2(regwriter_1_d2),
    .EN_3(regwriter_1_en_3), .D3(regwriter_1_d3), .EN_4(regwriter_1_en_4), .D4(regwriter_1_d4),
    .EN_5(regwriter_1_en_5), .D5(regwriter_1_d5), .EN_6(regwriter_1_en_6), .D6(regwriter_1_d6),
    .EN_7(regwriter_1_en_7), .D7(regwriter_1_d7), .EN_8(regwriter_1_en_8));
  Register #(.width(32)) register_1 (
    .D(regwriter_1_d0), .en(regwriter_1_en), .Q(register_1_q), .clk(clock), .clr(regreader_1_clr));
  Register #(.width(32)) register_2 (
    .D(regwriter_1_d1), .en(regwriter_1_en_2), .Q(register_2_q), .clk(clock), .clr(regreader_1_clr_2));
  Register #(.width(32)) register_3 (
    .D(regwriter_1_d2), .en(regwriter_1_en_3), .Q(register_3_q), .clk(clock), .clr(regreader_1_clr_3));
  Register #(.width(32)) register_4 (
    .D(regwriter_1_d3), .en(regwriter_1_en_4), .Q(register_4_q), .clk(clock), .clr(regreader_1_clr_4));
  Register #(.width(32)) register_5 (
    .D(regwriter_1_d4), .en(regwriter_1_en_5), .Q(register_5_q), .clk(clock), .clr(regreader_1_clr_5));
  Register #(.width(32)) register_6 (
    .D(regwriter_1_d5), .en(regwriter_1_en_6), .Q(register_6_q), .clk(clock), .clr(regreader_1_clr_6));
  Register #(.width(32)) register_7 (
    .D(regwriter_1_d6), .en(regwriter_1_en_7), .Q(register_7_q), .clk(clock), .clr(regreader_1_clr_7));
  Register #(.width(32)) register_8 (
    .D(regwriter_1_d7), .en(regwriter_1_en_8), .Q(register_8_q), .clk(clock), .clr(regreader_1_clr_8));
  regreader regreader_1 (
    .srcA(srcA), .srcB(srcB), .valA(valA), .valB(valB), .reset(clr), .CLR(regreader_1_clr), .Q(register_1_q),
    .CLR_2(regreader_1_clr_2), .Q_2(register_2_q), .CLR_3(regreader_1_clr_3), .Q_3(register_3_q),
    .CLR_4(regreader_1_clr_4), .Q_4(register_4_q), .CLR_5(regreader_1_clr_5), .Q_5(register_5_q),
    .CLR_6(regreader_1_clr_6), .Q_6(register_6_q), .CLR_7(regreader_1_clr_7), .Q_7(register_7_q),
    .CLR_8(regreader_1_clr_8), .Q_8(register_8_q));

  // Notes on the sheet:
  //   D0
  //   en0
  //   D7
  //   en7
  //   R0
  //   R1
  //   R2
  //   R3
  //   R4
  //   R5
  //   R6
  //   R7
  //   Q0
  //   clr0
  //   Q7
  //   clr7
endmodule

module regwriter (
  input  [2:0] dstE,
  input  reqE,
  input  [2:0] dstM,
  input  reqM,
  input  [31:0] valE,
  input  [31:0] valM,
  output [31:0] D0,
  output EN,
  output [31:0] D1,
  output EN_2,
  output [31:0] D2,
  output EN_3,
  output [31:0] D3,
  output EN_4,
  output [31:0] D4,
  output EN_5,
  output [31:0] D5,
  output EN_6,
  output [31:0] D6,
  output EN_7,
  output [31:0] D7,
  output EN_8
);

  wire [1:0] demultiplexer_3_out0, demultiplexer_3_out1, demultiplexer_3_out2, demultiplexer_3_out3,
       demultiplexer_3_out4, demultiplexer_3_out5, demultiplexer_3_out6, demultiplexer_3_out7;
  wire [31:0] demultiplexer_1_out0, demultiplexer_1_out1, demultiplexer_1_out2, demultiplexer_1_out3,
       demultiplexer_1_out4, demultiplexer_1_out5, demultiplexer_1_out6, demultiplexer_1_out7,
       demultiplexer_2_out0, demultiplexer_2_out1, demultiplexer_2_out2, demultiplexer_2_out3,
       demultiplexer_2_out4, demultiplexer_2_out5, demultiplexer_2_out6, demultiplexer_2_out7;

  Demultiplexer #(.select(3), .width(32)) demultiplexer_1 (
    .out0(demultiplexer_1_out0), .out1(demultiplexer_1_out1), .out2(demultiplexer_1_out2),
    .out3(demultiplexer_1_out3), .out4(demultiplexer_1_out4), .out5(demultiplexer_1_out5),
    .out6(demultiplexer_1_out6), .out7(demultiplexer_1_out7), .in(valE), .sel(dstE));  // open: en
  Demultiplexer #(.select(3), .width(32)) demultiplexer_2 (
    .out0(demultiplexer_2_out0), .out1(demultiplexer_2_out1), .out2(demultiplexer_2_out2),
    .out3(demultiplexer_2_out3), .out4(demultiplexer_2_out4), .out5(demultiplexer_2_out5),
    .out6(demultiplexer_2_out6), .out7(demultiplexer_2_out7), .in(valM), .sel(dstM));  // open: en
  Demultiplexer #(.select(3)) demultiplexer_3 (
    .out0(demultiplexer_3_out0[0]), .out1(demultiplexer_3_out1[0]), .out2(demultiplexer_3_out2[0]),
    .out3(demultiplexer_3_out3[0]), .out4(demultiplexer_3_out4[0]), .out5(demultiplexer_3_out5[0]),
    .out6(demultiplexer_3_out6[0]), .out7(demultiplexer_3_out7[0]), .in(reqE), .sel(dstE));  // open: en
  Demultiplexer #(.select(3)) demultiplexer_4 (
    .out0(demultiplexer_3_out0[1]), .out1(demultiplexer_3_out1[1]), .out2(demultiplexer_3_out2[1]),
    .out3(demultiplexer_3_out3[1]), .out4(demultiplexer_3_out4[1]), .out5(demultiplexer_3_out5[1]),
    .out6(demultiplexer_3_out6[1]), .out7(demultiplexer_3_out7[1]), .in(reqM), .sel(dstM));  // open: en
  Multiplexer #(.select(2), .width(32), .enable("false")) multiplexer_1 (
    .in1(demultiplexer_1_out0), .in2(demultiplexer_2_out0), .out(D0), .sel(demultiplexer_3_out0));  // open: in0, in3
  Multiplexer #(.select(2), .width(32), .enable("false")) multiplexer_2 (
    .in1(demultiplexer_1_out1), .in2(demultiplexer_2_out1), .out(D1), .sel(demultiplexer_3_out1));  // open: in0, in3
  Multiplexer #(.select(2), .width(32), .enable("false")) multiplexer_3 (
    .in1(demultiplexer_1_out2), .in2(demultiplexer_2_out2), .out(D2), .sel(demultiplexer_3_out2));  // open: in0, in3
  Multiplexer #(.select(2), .width(32), .enable("false")) multiplexer_4 (
    .in1(demultiplexer_1_out3), .in2(demultiplexer_2_out3), .out(D3), .sel(demultiplexer_3_out3));  // open: in0, in3
  Multiplexer #(.select(2), .width(32), .enable("false")) multiplexer_5 (
    .in1(demultiplexer_1_out4), .in2(demultiplexer_2_out4), .out(D4), .sel(demultiplexer_3_out4));  // open: in0, in3
  Multiplexer #(.select(2), .width(32), .enable("false")) multiplexer_6 (
    .in1(demultiplexer_1_out5), .in2(demultiplexer_2_out5), .out(D5), .sel(demultiplexer_3_out5));  // open: in0, in3
  Multiplexer #(.select(2), .width(32), .enable("false")) multiplexer_7 (
    .in1(demultiplexer_1_out6), .in2(demultiplexer_2_out6), .out(D6), .sel(demultiplexer_3_out6));  // open: in0, in3
  Multiplexer #(.select(2), .width(32), .enable("false")) multiplexer_8 (
    .in1(demultiplexer_1_out7), .in2(demultiplexer_2_out7), .out(D7), .sel(demultiplexer_3_out7));  // open: in0, in3
  xor xor_1 (EN, demultiplexer_3_out0[0], demultiplexer_3_out0[1]);
  xor xor_2 (EN_2, demultiplexer_3_out1[0], demultiplexer_3_out1[1]);
  xor xor_3 (EN_3, demultiplexer_3_out2[0], demultiplexer_3_out2[1]);
  xor xor_4 (EN_4, demultiplexer_3_out3[0], demultiplexer_3_out3[1]);
  xor xor_5 (EN_5, demultiplexer_3_out4[0], demultiplexer_3_out4[1]);
  xor xor_6 (EN_6, demultiplexer_3_out5[0], demultiplexer_3_out5[1]);
  xor xor_7 (EN_7, demultiplexer_3_out6[0], demultiplexer_3_out6[1]);
  xor xor_8 (EN_8, demultiplexer_3_out7[0], demultiplexer_3_out7[1]);
endmodule

module regreader (
  input  [2:0] srcA,
  input  [2:0] srcB,
  input  [31:0] Q,
  input  [31:0] Q_2,
  input  [31:0] Q_3,
  input  reset,
  input  [31:0] Q_4,
  input  [31:0] Q_5,
  input  [31:0] Q_6,
  input  [31:0] Q_7,
  input  [31:0] Q_8,
  output CLR,
  output [31:0] valA,
  output [31:0] valB,
  output CLR_2,
  output CLR_3,
  output CLR_4,
  output CLR_5,
  output CLR_6,
  output CLR_7,
  output CLR_8
);

  Multiplexer #(.select(3), .width(32), .enable("false")) multiplexer_1 (
    .in0(Q), .in1(Q_2), .in2(Q_3), .in3(Q_4), .in4(Q_5), .in5(Q_6), .in6(Q_7), .in7(Q_8), .out(valA),
    .sel(srcA));
  Multiplexer #(.select(3), .width(32), .enable("false")) multiplexer_2 (
    .in0(Q), .in1(Q_2), .in2(Q_3), .in3(Q_4), .in4(Q_5), .in5(Q_6), .in6(Q_7), .in7(Q_8), .out(valB),
    .sel(srcB));

  assign CLR = reset;
  assign CLR_2 = reset;
  assign CLR_3 = reset;
  assign CLR_4 = reset;
  assign CLR_5 = reset;
  assign CLR_6 = reset;
  assign CLR_7 = reset;
  assign CLR_8 = reset;

  // Notes on the sheet:
  //   for reg 0
  //   for reg 7
endmodule
