// Logisim project HW3Q4.circ as structural Verilog: 1 circuit, main circuit main
module main (
  input  [31:0] aluA,
  input  [31:0] aluB,
  input  [3:0] aluOP,
  output [2:0] CC__Z_S_O,
  output [31:0] valE
);

  wire adder_1_cout, subtractor_1_bout;
  wire [31:0] adder_1_out, and_1_out, subtractor_1_out, xor_1_out;

  Adder #(.width(32)) adder_1 (.a(aluB), .b(aluA), .out(adder_1_out), .cout(adder_1_cout));  // open: cin
  Subtractor #(.width(32)) subtractor_1 (
    .a(aluB), .b(aluA), .out(subtractor_1_out), .bout(subtractor_1_bout));  // open: bin
  assign and_1_out = aluB & aluA;  // AND_Gate and_1, 32 bits wide
  assign xor_1_out = aluB ^ aluA;  // XOR_Gate xor_1, 32 bits wide
  Multiplexer #(.select(2)) multiplexer_1 (
    .in0(adder_1_cout), .in1(subtractor_1_bout), .in2(1'b0), .in3(1'b0), .out(CC__Z_S_O[0]), .sel(aluOP[1:0]));  // open: en
  Multiplexer #(.select(2), .width(32)) multiplexer_2 (
    .in0(adder_1_out), .in1(subtractor_1_out), .in2(and_1_out), .in3(xor_1_out),
    .out({CC__Z_S_O[1], valE[30:0]}), .sel(aluOP[1:0]));  // open: en
  Comparator #(.width(32), .mode("unsigned")) comparator_1 (
    .a({32{1'b0}}), .b({CC__Z_S_O[1], valE[30:0]}), .eq(CC__Z_S_O[2]));  // open: gt, lt

  assign valE[31] = CC__Z_S_O[1];

  // Notes on the sheet:
  //   addl [00]
  //   subl [01]
  //   andl [10]
  //   xorl [11]
  //   Determine overflow only for addl and subl
  //   determine if negative (if most significant bit high)
  //   determine if equal to zero
endmodule
