// Logisim project HW3Q4v2.circ as structural Verilog: 1 circuit, main circuit main
module main (
  input  [31:0] aluA,
  input  [31:0] aluB,
  input  [3:0] aluOP,
  output [2:0] CC__Z_S_O,
  output [31:0] valE
);

  wire and_1_out, and_2_out, and_3_out, and_4_out, multiplexer_1_out, multiplexer_2_out, not_1_out,
       not_2_out, or_1_out;
  wire [31:0] adder_1_out, and_5_out, subtractor_1_out, xor_1_out;

  Multiplexer multiplexer_1 (.in0(aluA[31]), .in1(not_1_out), .out(multiplexer_1_out), .sel(aluOP[0]));  // open: en
  not not_1 (not_1_out, aluA[31]);
  Multiplexer multiplexer_2 (.in0(aluA[31]), .in1(not_2_out), .out(multiplexer_2_out), .sel(aluOP[0]));  // open: en
  not not_2 (not_2_out, aluA[31]);
  and and_1 (and_1_out, multiplexer_1_out, aluB[31]);
  and and_2 (and_2_out, ~multiplexer_2_out, ~aluB[31]);  // AND_Gate
  and and_3 (and_3_out, and_1_out, ~CC__Z_S_O[1]);  // AND_Gate
  and and_4 (and_4_out, CC__Z_S_O[1], and_2_out);
  or or_1 (or_1_out, and_3_out, and_4_out);
  Adder #(.width(32)) adder_1 (.a(aluB), .b(aluA), .out(adder_1_out));  // open: cin, cout
  Subtractor #(.width(32)) subtractor_1 (.a(aluB), .b(aluA), .out(subtractor_1_out));  // open: bin, bout
  assign and_5_out = aluB & aluA;  // AND_Gate and_5, 32 bits wide
  assign xor_1_out = aluB ^ aluA;  // XOR_Gate xor_1, 32 bits wide
  Multiplexer multiplexer_3 (.in0(or_1_out), .in1(1'b0), .out(CC__Z_S_O[0]), .sel(aluOP[1]));  // open: en
  Multiplexer #(.select(2), .width(32)) multiplexer_4 (
    .in0(adder_1_out), .in1(subtractor_1_out), .in2(and_5_out), .in3(xor_1_out),
    .out({CC__Z_S_O[1], valE[30:0]}), .sel(aluOP[1:0]));  // open: en
  Comparator #(.width(32), .mode("unsigned")) comparator_1 (
    .a({32{1'b0}}), .b({CC__Z_S_O[1], valE[30:0]}), .eq(CC__Z_S_O[2]));  // open: gt, lt

  assign valE[31] = CC__Z_S_O[1];

  // Notes on the sheet:
  //   determine overflow flag:
  //   addl [00]
  //   subl [01]
  //   xorl [11]
  //   Determine overflow only for addl and subl
  //   determine if negative (if most significant bit high)
  //   determine if equal to zero
endmodule
