// Logisim project HW4Q1.circ as structural Verilog: 1 circuit, main circuit main
module main (
  input  [2:0] ZSO,
  input  [3:0] ifun,
  output out_3
);

  wire and_1_out, not_1_out, not_2_out, or_1_out, xor_1_out;

  xor xor_1 (xor_1_out, ZSO[1], ZSO[0]);
  not not_1 (not_1_out, xor_1_out);
  or or_1 (or_1_out, ZSO[2], xor_1_out);
  not not_2 (not_2_out, ZSO[2]);
  and and_1 (and_1_out, not_2_out, not_1_out);
  Multiplexer #(.select(4)) multiplexer_1 (
    .in0(1'b1), .in1(or_1_out), .in2(xor_1_out), .in3(ZSO[2]), .in4(not_2_out), .in5(not_1_out),
    .in6(and_1_out), .in7(1'b0), .in8(1'b0), .in9(1'b0), .in10(1'b0), .in11(1'b0), .in12(1'b0), .in13(1'b0),
    .in14(1'b0), .in15(1'b0), .out(out_3), .sel(ifun));  // open: en
endmodule
