// Logisim project HW5Q2.circ as structural Verilog: 2 circuits, main circuit io
module io (
  input  KB_Status,
  input  [6:0] in_2,
  input  RAM_Use,
  input  [31:0] in_4,
  input  [7:0] in_5,
  input  RAM_Read,
  input  RAM_Write,
  input  TTY_Ready,
  input  reset,
  output KB_Clock,
  output KB_Clear,
  output [7:0] out_12,
  output [6:0] out_13,
  output TTY_Enable,
  output TTY_Clear
);

  wire and_1_out, and_2_out, comparator_1_eq, comparator_2_eq, comparator_3_eq, comparator_4_eq,
       comparator_5_eq, nor_1_out;
  wire [7:0] bit_extender_1_out, bit_extender_2_out, bit_extender_3_out, controlled_buffer_1_out,
       controlled_buffer_5_out, register_1_q;

  Comparator #(.width(32)) comparator_1 (.a(32'hfffe00), .b(in_4), .eq(comparator_1_eq));  // open: gt, lt
  and and_1 (and_1_out, RAM_Use, RAM_Read);
  and and_2 (and_2_out, RAM_Use, RAM_Write);
  Comparator #(.width(32)) comparator_2 (.a(32'hfffe04), .b(in_4), .eq(comparator_2_eq));  // open: gt, lt
  Comparator #(.width(32)) comparator_3 (.a(32'hfffe08), .b(in_4), .eq(comparator_3_eq));  // open: gt, lt
  Comparator #(.width(32)) comparator_4 (.a(32'hfffe0c), .b(in_4), .eq(comparator_4_eq));  // open: gt, lt
  assign bit_extender_1_out = {{1{1'b0}}, in_2};  // Bit_Extender bit_extender_1
  assign controlled_buffer_1_out = nor_1_out ? {8{1'b0}} : 8'bz;  // Controlled_Buffer controlled_buffer_1
  nor nor_1 (nor_1_out, comparator_1_eq, comparator_2_eq, comparator_3_eq, comparator_4_eq);
  and and_3 (TTY_Enable, comparator_4_eq, and_2_out);
  Register register_1 (.D(bit_extender_1_out), .Q(register_1_q), .clk(KB_Clock));  // open: en, clr
  assign bit_extender_2_out = {{7{1'b0}}, KB_Status};  // Bit_Extender bit_extender_2
  assign controlled_buffer_1_out = comparator_1_eq ? bit_extender_2_out : 8'bz;  // Controlled_Buffer controlled_buffer_2
  assign controlled_buffer_1_out = comparator_2_eq ? register_1_q : 8'bz;  // Controlled_Buffer controlled_buffer_3
  assign bit_extender_3_out = {{7{1'b0}}, TTY_Ready};  // Bit_Extender bit_extender_3
  Bit_Extender #(.out_width(7)) bit_extender_4 (.in(in_5), .out(out_13));
  and and_4 (KB_Clock, comparator_2_eq, and_1_out);
  assign controlled_buffer_1_out = comparator_3_eq ? bit_extender_3_out : 8'bz;  // Controlled_Buffer controlled_buffer_4
  Comparator #(.width(24)) comparator_5 (.a(24'hfffe), .b(in_4[31:8]), .eq(comparator_5_eq));  // open: gt, lt
  assign controlled_buffer_5_out = and_1_out ? controlled_buffer_1_out : 8'bz;  // Controlled_Buffer controlled_buffer_5
  assign out_12 = comparator_5_eq ? controlled_buffer_5_out : 8'bz;  // Controlled_Buffer controlled_buffer_6

  assign KB_Clear = reset;
  assign TTY_Clear = reset;

  // Notes on the sheet:
  //   RAM Address
  //   Incoming Data
  //   KB Data
  //   Outgoing Data
  //   TTY Data
endmodule

module test (
  input  Use_RAM__please,
  input  [31:0] address,
  input  [7:0] data_to__RAM,
  input  read,
  input  write,
  input  in_6
);

  wire clock_out, io_1_kb_clear, io_1_kb_clock, io_1_tty_clear, io_1_tty_enable, keyboard_1_avail, reset_out;
  wire [6:0] io_1_out_13, keyboard_1_data;
  wire [7:0] io_1_out_12;

  // Probe on address
  // Probe on io_1_out_12
  Button reset (.out(reset_out));
  Button clock (.out(clock_out));
  // Probe on data_to__RAM
  io io_1 (
    .RAM_Use(Use_RAM__please), .in_4(address), .in_5(data_to__RAM), .RAM_Read(read), .RAM_Write(write),
    .out_12(io_1_out_12), .TTY_Ready(in_6), .in_2(keyboard_1_data), .KB_Status(keyboard_1_avail),
    .KB_Clock(io_1_kb_clock), .out_13(io_1_out_13), .reset(reset_out), .KB_Clear(io_1_kb_clear),
    .TTY_Clear(io_1_tty_clear), .TTY_Enable(io_1_tty_enable));
  Keyboard keyboard_1 (
    .clk(io_1_kb_clock), .re(1'b1), .clr(io_1_kb_clear), .avail(keyboard_1_avail), .data(keyboard_1_data));
  TTY tty_1 (.data(io_1_out_13), .clk(clock_out), .we(io_1_tty_enable), .clr(io_1_tty_clear));
endmodule
