// Logisim project HW5Q3.circ as structural Verilog: 1 circuit, main circuit main
module main (
  input  [5:0] CurrentState,
  input  [1:0] Select,
  input  [3:0] icode,
  input  [5:0] valN,
  input  DMemDone,
  input  IMemDone,
  output [5:0] NextState
);

  wire [5:0] bit_extender_1_out, multiplexer_1_out, multiplexer_2_out;

  assign bit_extender_1_out = {{2{1'b1}}, icode};  // Bit_Extender bit_extender_1
  Multiplexer #(.width(6)) multiplexer_1 (
    .in0(CurrentState), .in1(valN), .out(multiplexer_1_out), .sel(DMemDone));  // open: en
  Multiplexer #(.width(6)) multiplexer_2 (
    .in0(CurrentState), .in1(bit_extender_1_out), .out(multiplexer_2_out), .sel(IMemDone));  // open: en
  Multiplexer #(.select(2), .width(6)) multiplexer_3 (
    .in0(CurrentState), .in1(valN), .in2(multiplexer_1_out), .in3(multiplexer_2_out), .out(NextState),
    .sel(Select));  // open: en
endmodule
