// Logisim project hw9q5.circ as structural Verilog: 1 circuit, main circuit main
module main (
  input  [15:0] Addr,
  input  RAM_Use,
  input  RAM_Read,
  input  RAM_Write,
  input  Priv,
  output [15:0] Addr_Out,
  output VALID,
  output UNPRIV_READ,
  output UNPRIV_WRITE,
  output RAM_Use_2,
  output RAM_Read_2,
  output Ram_Write_2,
  output Trap
);

  wire and_1_out, and_2_out, and_3_out, or_1_out, or_2_out, or_3_out, or_4_out;

  or or_1 (or_1_out, RAM_Read, RAM_Write);
  and and_1 (and_1_out, or_1_out, RAM_Use);
  RAM #(.dataWidth(3)) ram_1 (
    .addr(Addr[15:8]), .data({UNPRIV_WRITE, UNPRIV_READ, VALID}), .sel(1'b1));  // open: clk, ld, clr
  or or_2 (or_2_out, UNPRIV_READ, ~Priv);  // OR_Gate
  or or_3 (or_3_out, UNPRIV_WRITE, ~Priv);  // OR_Gate
  and and_2 (and_2_out, RAM_Read, ~or_2_out);  // AND_Gate
  RAM ram_2 (.addr(Addr[15:8]), .data(Addr_Out[15:8]), .sel(1'b1));  // open: clk, ld, clr
  and and_3 (and_3_out, RAM_Write, ~or_3_out);  // AND_Gate
  and and_4 (RAM_Read_2, or_2_out, RAM_Use, RAM_Read, VALID);
  and and_5 (Ram_Write_2, or_3_out, RAM_Use, RAM_Write, VALID);
  or or_4 (or_4_out, and_2_out, and_3_out, ~VALID);  // OR_Gate
  and and_6 (RAM_Use_2, or_1_out, RAM_Use, ~Trap);  // AND_Gate
  and and_7 (Trap, and_1_out, or_4_out);

  assign Addr_Out[7:0] = Addr[7:0];
endmodule
